# Fritzing sketch DIY Group Project (saved by Fritzing 0.9.3b)

parts:
  Part1 = Arduino Uno (Rev3)
  U1 = LCD-16X2 [package=lcd-16x2_nosilk]
  LCM1602_IIC1 = LCM1602 IIC [part_number="LCM1602 IIC" chip_label="LCM1602 IIC" package="DIP (Dual Inline) [THT]"]
  M1 = fc-51 [package=THT]
  SIM800L_BO1 = SIM800L BO
  M2 = RioRand LM2596
  Part2 = Jtron 1 Channel Optoisolated Relay Module [package=relay]
  Keypad4x1 = Keypad Membran 4x4
  VALVE1 = Plastic Solenoid Valve
  BAT1 = BC9VPC [package=bc9vpc]
  VCC1 = Battery block 9V

nets:
  N1: Part1.A0, M1.pin1
  N2: Part1.A4/SDA, LCM1602_IIC1.SDA
  N3: Part1.A5/SCL, LCM1602_IIC1.SCL
  N4: Part1.D8, Keypad4x1.Pin6
  N5: Part1.D9_PWM, Keypad4x1.Pin5
  N6: Part1.D10_PWM/SS, Keypad4x1.Pin4
  N7: Part1.D11_PWM/MOSI, Keypad4x1.Pin3
  N8: Part1.D12/MISO, Keypad4x1.Pin2
  N9: Part1.D13/SCK, Keypad4x1.Pin1
  N10: Part1.D2, SIM800L_BO1.pin_4
  N11: Part1.D3_PWM, SIM800L_BO1.pin_5
  N12: Part1.D4, Part2.IN1
  N13: Part1.D6_PWM, Keypad4x1.Pin8
  N14: Part1.D7, Keypad4x1.Pin7
  VCC: Part1.5V, LCM1602_IIC1.VCC, M1.pin3, Part2.VCC
  GND: Part1.GND, LCM1602_IIC1.GND, M1.pin2, Part2.GND
  VSS: U1.VSS, LCM1602_IIC1.VSS
  VDD: U1.VDD, LCM1602_IIC1.VDD
  N15: U1.VO, LCM1602_IIC1.V0
  N16: U1.RS, LCM1602_IIC1.RS
  N17: U1.R_W, LCM1602_IIC1.RW
  N18: U1.E, LCM1602_IIC1.E
  N19: U1.DB0, LCM1602_IIC1.D0
  N20: U1.DB1, LCM1602_IIC1.D1
  N21: U1.DB2, LCM1602_IIC1.D2
  N22: U1.DB3, LCM1602_IIC1.D3
  N23: U1.DB4, LCM1602_IIC1.D4
  N24: U1.DB5, LCM1602_IIC1.D5
  N25: U1.DB6, LCM1602_IIC1.D6
  N26: U1.DB7, LCM1602_IIC1.D7
  N27: U1.A, LCM1602_IIC1.A
  N28: U1.K, LCM1602_IIC1.K
  N29: SIM800L_BO1.PIN2, M2.Pin_3
  N30: SIM800L_BO1.pin_6, M2.Pin_4
  N31: M2.Pin_1, BAT1.V+
  N32: M2.Pin_2, BAT1.V-
  N33: Part2.NO, VCC1.+
  N34: Part2.MAIN, VALVE1.no_name_yet#1
  N35: VALVE1.no_name_yet#2, VCC1.-

notes:
  OTP Based Smart Door Lock
  Circuit Design by
  Harshith and Adarsh

custom parts:
  LCM1602 IIC: I2C-Module to use a 1602 or 2004 LCD on with the wire.h libory Serial LCD Modul
  Keypad Membran 4x4: Membrane Keypad 4x4 Matrix

// code stored in the sketch: Code.ino
#include <SoftwareSerial.h>
#include <Wire.h>
#include <LiquidCrystal_I2C.h>
#include <Keypad.h>
#define relay 4
#define red 16
#define green 15

const byte ROWS = 4;
const byte COLS = 4;
char hexaKeys[ROWS][COLS] = {
  {'1', '2', '3', 'A'},
  {'4', '5', '6', 'B'},
  {'7', '8', '9', 'C'},
  {'*', '0', '#', 'D'}
};
byte rowPins[ROWS] = {13, 12, 11, 10};
byte colPins[COLS] = {9, 8, 7, 6};
Keypad customKeypad = Keypad( makeKeymap(hexaKeys), rowPins, colPins, ROWS, COLS);

LiquidCrystal_I2C lcd(0x27, 16, 2);

SoftwareSerial sim800l(3, 2);
int irsensor = A0;
int otp;
String otpstring = "";
int i = 0;
void setup()
{

  pinMode(irsensor, INPUT_PULLUP);
  sim800l.begin(4800);
  Serial.begin(115200);
  lcd.init();
  lcd.backlight();
  Serial.print("Welcome to SIM800L Project");
  sim800l.println("AT");
  updateSerial();
  pinMode(relay, OUTPUT);
  pinMode(red, INPUT);
  pinMode(green, INPUT);
  digitalWrite(relay, LOW);
  delay(500);
  sim800l.println("AT+CSQ");
  updateSerial();
  delay(1000);

}
void updateSerial()
{
  delay(500);
  while (Serial.available()) {
    sim800l.write(Serial.read());
  }
  while (sim800l.available()) {
    Serial.write(sim800l.read());
  }
}
void loop()
{
  lcd.setCursor(0, 0);
  lcd.print("   OTP Based");
  lcd.setCursor(0, 1);
  lcd.print("   Door Lock");
  if (digitalRead(irsensor) == LOW)
  {
    otp = random(2000, 9999);
    otpstring = String(otp);
    Serial.println(otpstring);
    while (digitalRead(irsensor) == LOW) {}
    lcd.clear();
    lcd.setCursor(0, 0);
    lcd.print(" OTP Sent to");
    lcd.setCursor(0, 1);
    lcd.print(" Your Mobile");
    Serial.print("OTP is ");
    delay(100);
    Serial.println(otpstring);
    delay(100);
    SendSMS();
    lcd.clear();
    lcd.setCursor(0, 0);
    lcd.print("Enter OTP :");
    getotp();
  }

}

void getotp() {

  String y = "";
  int a = y.length();
  while (a < 4)
  {
    char customKey = customKeypad.getKey();
    if (customKey) {
      lcd.setCursor(0, 1);
      y = y + customKey;
      lcd.print(y);
      a = y.length();
    }
  }
  Serial.print("Entered OTP is ");
  Serial.println(y);
  if (otpstring == y)
  {
    lcd.setCursor(0, 0);
    lcd.print("Access Granted");
    lcd.setCursor(0, 1);
    lcd.print("Door Opening");
    digitalWrite(relay, HIGH);
    digitalWrite(red, HIGH);
    digitalWrite(green, LOW);
    delay(5000);
    digitalWrite(relay, LOW);
    digitalWrite(red, LOW);
    digitalWrite(green, HIGH);
  }
  else
  {
    lcd.setCursor(0, 0);
    lcd.print("Access Failed");
    lcd.setCursor(0, 1);
    lcd.print("Try Again !!!");
    delay(3000);
  }


}
void SendSMS()
{
  Serial.println("Sending SMS...");
  sim800l.print("AT+CMGF=1\r");
  delay(100);
  sim800l.print ("AT+CSMP=17,167,0,0\r");
  delay(500);
  sim800l.print("AT+CMGS=\"+91xxxxxxxxxxx\"\r");
  delay(500);
  sim800l.print("Your OTP is " + otpstring + " Just Type OTP And Unlock The Door");
  delay(500);
  sim800l.print((char)26);
  delay(500);
  sim800l.println();
  Serial.println("Text Sent.");
  delay(500);

}
